# Fritzing sketch circuit (saved by Fritzing 0.9.10b)
breadboards: 1

parts:
  S2 = Pushbutton [package="[THT]"]
  SM1 = 28BYJ-48 Stepper Motor [part_number=28BYJ-48]  # not connected
  Driver1 = 28BYJ-48 Driver Module [part_number=ULN2003 package=THT]
  OLED1 = OLED 128x64 I2C Monochrome Display GND-VDD
  S3 = Pushbutton [package="[THT]"]
  S4 = Pushbutton [package="[THT]"]
  Componente1 = Arduino Uno (Rev3)
  ZS-042_RTC1 = ZS-042 RTC Module

nets:
  GND: S2.Pin_1, S2.Pin_2, Driver1.GND, OLED1.GND, S3.Pin_1, S3.Pin_2, S4.Pin_1, S4.Pin_2, Componente1.GND, ZS-042_RTC1.GND
  N1: S2.Pin_3, S2.Pin_4, Componente1.D4
  N2: Driver1.IN1, Componente1.D8
  N3: Driver1.IN2, Componente1.D9_PWM
  N4: Driver1.IN3, Componente1.D10_PWM/SS
  N5: Driver1.IN4, Componente1.D11_PWM/MOSI
  VDD: Driver1.Vmotor, OLED1.VDD, Componente1.5V, ZS-042_RTC1.VCC
  N6: OLED1.SCK, Componente1.A4/SDA, ZS-042_RTC1.SCL
  N7: OLED1.SDA, Componente1.A5/SCL, ZS-042_RTC1.SDA
  N8: S3.Pin_3, S3.Pin_4, Componente1.D5_PWM
  N9: S4.Pin_3, S4.Pin_4, Componente1.D6_PWM

custom parts:
  28BYJ-48 Stepper Motor: Unipolar Stepper Motor 28BYJ-48 Top coil - pink & orange Bottom coil - blue & yellow Common rail - red Connector pins: blue - pink - yellow - orange - red
  28BYJ-48 Driver Module: High-power ULN2003 Stepper Motor Driver Board Test Module For Arduino AVR SMD
  OLED 128x64 I2C Monochrome Display GND-VDD: OLED 128x64 I2C Monochrome Display. Note: there are two variants of this part, this one is the GND VDD SCK SDA variant. The other is VDD GND SCK SDA. Make sure you select the part that matches your module as using the incorrect part will probably destroy your module! In addition the mounting holes are marked on silkscreen but not by default drilled. If you want drilled mounting holes, copy a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
